// Logisim project S2-T5-Hardware-Logisim.circ as structural Verilog: 4 circuits, main circuit main
module main (
  input  ACTIVITY_0,
  input  ACTIVITY_1,
  input  RESET,
  input  D1,
  input  D0,
  output S1,
  output S0
);

  wire and_1_out, and_2_out, and_3_out, and_4_out, and_5_out, and_6_out, Clk_out, j_k_ff_1_q, j_k_ff_2_q,
       not_1_out, not_2_out, not_3_out, or_1_out;

  Clock Clk (.out(Clk_out));
  or or_1 (or_1_out, ACTIVITY_0, ACTIVITY_1);
  and and_1 (and_1_out, D1, not_1_out, not_2_out);
  and and_2 (and_2_out, or_1_out, Clk_out);
  and and_3 (and_3_out, D1, not_2_out, j_k_ff_1_q);
  and and_4 (and_4_out, and_1_out, not_3_out);
  or or_2 (S1, and_4_out, and_3_out);
  not not_1 (not_1_out, D0);
  and and_5 (and_5_out, D1, D0, j_k_ff_2_q);
  J_K_Flip_Flop #(.trigger("falling")) j_k_ff_1 (
    .J(1'b1), .clk(and_2_out), .K(1'b1), .Q(j_k_ff_1_q), .reset(RESET));  // open: Qn, preset, en
  not not_2 (not_2_out, j_k_ff_2_q);
  not not_3 (not_3_out, j_k_ff_1_q);
  and and_6 (and_6_out, D0, not_2_out, j_k_ff_1_q);
  or or_3 (S0, and_5_out, and_6_out);
  J_K_Flip_Flop #(.trigger("falling")) j_k_ff_2 (
    .J(1'b1), .clk(j_k_ff_1_q), .K(1'b1), .Q(j_k_ff_2_q), .reset(RESET));  // open: Qn, preset, en
endmodule

module SEQUENTIAL_SPEED_CALCULATOR (
  input  ACTIVITY_0,
  input  ACTIVITY_1,
  input  RESET,
  input  D1,
  input  D0,
  output S1,
  output S0
);

  wire and_1_out, and_3_out, and_4_out, Clk_out, j_k_ff_1_q, j_k_ff_2_q, not_1_out, not_2_out, or_1_out;

  Clock Clk (.out(Clk_out));
  or or_1 (or_1_out, ACTIVITY_0, ACTIVITY_1);
  and and_1 (and_1_out, or_1_out, Clk_out);
  and and_2 (S1, D1, not_1_out, j_k_ff_1_q);
  J_K_Flip_Flop #(.trigger("falling")) j_k_ff_1 (
    .J(1'b1), .clk(and_1_out), .K(1'b1), .Q(j_k_ff_1_q), .reset(RESET));  // open: Qn, preset, en
  not not_1 (not_1_out, j_k_ff_2_q);
  and and_3 (and_3_out, D0, not_1_out, j_k_ff_1_q);
  or or_2 (S0, and_3_out, and_4_out);
  J_K_Flip_Flop #(.trigger("falling")) j_k_ff_2 (
    .J(1'b1), .clk(j_k_ff_1_q), .K(1'b1), .Q(j_k_ff_2_q), .reset(RESET));  // open: Qn, preset, en
  not not_2 (not_2_out, j_k_ff_1_q);
  and and_4 (and_4_out, j_k_ff_2_q, D1, not_2_out);

  // Notes on the sheet:
  //   SEQUENTIAL-SPEED CALCULATOR
endmodule

module CALORIE_CALCULATOR (
  input  in_1,
  input  in_2,
  input  in_3,
  input  in_4,
  input  in_5,
  input  in_6,
  output out_7,
  output out_8,
  output out_9,
  output out_10,
  output out_11,
  output out_12
);

  wire and_1_out, and_2_out, and_3_out, and_4_out, and_5_out, and_6_out, and_7_out, and_8_out, and_9_out,
       and_10_out, and_11_out, D0, D1, n4bitadder_2_out_11, n4bitadder_2_out_12, n4bitadder_2_out_13,
       not_1_out;

  and and_1 (and_1_out, D1, n4bitadder_2_out_11);
  and and_2 (and_2_out, D1, n4bitadder_2_out_12);
  and and_3 (and_3_out, in_1, in_3);
  and and_4 (and_4_out, D1, n4bitadder_2_out_13);
  and and_5 (and_5_out, D1, and_11_out);
  and and_6 (and_6_out, in_1, in_4);
  and and_7 (and_7_out, D0, n4bitadder_2_out_11);
  and and_8 (and_8_out, in_2, in_3);
  and and_9 (and_9_out, D0, n4bitadder_2_out_12);
  _4BitAdder u_4bitadder_1 (
    .a0(and_10_out), .b0(and_5_out), .a1(and_9_out), .b1(and_4_out), .a2(and_7_out), .b2(and_2_out),
    .a3(1'b0), .b3(and_1_out), .out_9(out_7), .out_10(out_8), .out_11(out_9), .out_12(out_10), .out_13(out_11));
  _4BitAdder u_4bitadder_2 (
    .a0(and_8_out), .b0(and_6_out), .a1(1'b0), .b1(and_3_out), .a2(1'b0), .b2(1'b0), .a3(1'b0), .b3(1'b0),
    .out_11(n4bitadder_2_out_11), .out_12(n4bitadder_2_out_12), .out_13(n4bitadder_2_out_13));  // open: out_9, out_10
  and and_10 (and_10_out, D0, n4bitadder_2_out_13);
  and and_11 (and_11_out, in_2, in_4);
  and and_12 (out_12, D0, and_11_out);
  xor xor_1 (D1, in_5, in_6);
  not not_1 (not_1_out, in_5);
  and and_13 (D0, not_1_out, in_6);

  // Other names for the same wires on the sheet: A0 = in_2; A1 = in_1; B0 = in_4; B1 = in_3; S0 = in_6; S1 = in_5

  // Notes on the sheet:
  //   CALORIE CALCULATOR
  //   MET CALCULATION
endmodule

module _4BitAdder (
  input  a0,
  input  b0,
  input  a1,
  input  b1,
  input  a2,
  input  b2,
  input  a3,
  input  b3,
  output out_9,
  output out_10,
  output out_11,
  output out_12,
  output out_13
);

  wire adder_1_cout, adder_2_cout, adder_3_cout;

  Adder #(.width(1)) adder_1 (.a(a0), .b(b0), .out(out_13), .cout(adder_1_cout));  // open: cin
  Adder #(.width(1)) adder_2 (.a(a1), .b(b1), .out(out_12), .cin(adder_1_cout), .cout(adder_2_cout));
  Adder #(.width(1)) adder_3 (.a(a2), .b(b2), .out(out_11), .cin(adder_2_cout), .cout(adder_3_cout));
  Adder #(.width(1)) adder_4 (.a(a3), .b(b3), .out(out_10), .cin(adder_3_cout), .cout(out_9));
endmodule
