// Logisim project S2-T5-ChronoFit.circ as structural Verilog: 10 circuits, main circuit Clock
// CLOCK
module Clock (
  input  ACTIVITY,
  input  RESET,
  output out_3,
  output out_4,
  output out_5,
  output out_6,
  output out_7,
  output out_8
);

  wire and_1_out, and_2_out, CLK_PULSE_out, or_1_out;

  Clock_part CLK_PULSE (.out(CLK_PULSE_out));
  and and_1 (and_1_out, ACTIVITY, CLK_PULSE_out);
  or or_1 (or_1_out, RESET, and_2_out);
  and and_2 (and_2_out, out_3, out_5, out_6, out_7, out_8);
  J_K_Flip_Flop #(.trigger("falling")) j_k_ff_1 (
    .J(1'b1), .clk(and_1_out), .K(1'b1), .Q(out_3), .preset(1'b0), .en(1'b1), .reset(or_1_out));  // open: Qn
  J_K_Flip_Flop #(.trigger("falling")) j_k_ff_2 (
    .J(1'b1), .clk(out_3), .K(1'b1), .Q(out_4), .preset(1'b0), .en(1'b1), .reset(or_1_out));  // open: Qn
  J_K_Flip_Flop #(.trigger("falling")) j_k_ff_3 (
    .J(1'b1), .clk(out_4), .K(1'b1), .Q(out_5), .preset(1'b0), .en(1'b1), .reset(or_1_out));  // open: Qn
  J_K_Flip_Flop #(.trigger("falling")) j_k_ff_4 (
    .J(1'b1), .clk(out_5), .K(1'b1), .Q(out_6), .preset(1'b0), .en(1'b1), .reset(or_1_out));  // open: Qn
  J_K_Flip_Flop #(.trigger("falling")) j_k_ff_5 (
    .J(1'b1), .clk(out_6), .K(1'b1), .Q(out_7), .preset(1'b0), .en(1'b1), .reset(or_1_out));  // open: Qn
  J_K_Flip_Flop #(.trigger("falling")) j_k_ff_6 (
    .J(1'b1), .clk(out_7), .K(1'b1), .Q(out_8), .preset(1'b0), .en(1'b1), .reset(or_1_out));  // open: Qn

  // Notes on the sheet:
  //   BASIC 60 seconds upcounter, used as a minute stopwatch
  //   Created using JK flip flops
  //   The counter resets when either the RESET button has been toggled or the counter reaches 60 seconds
  //   The clk pulse has been set at the frequency of 2Hz so that the counter is triggered every second
endmodule

// 8 BIT ADDER
module _8_bit_adder (
  input  in_1,
  input  in_2,
  input  in_3,
  input  in_4,
  input  in_5,
  input  in_6,
  input  in_7,
  input  in_8,
  input  in_9,
  input  in_10,
  input  in_11,
  input  in_12,
  input  in_13,
  input  in_14,
  input  in_15,
  input  in_16,
  input  in_17,
  output out_18,
  output out_19,
  output out_20,
  output out_21,
  output out_22,
  output out_23,
  output out_24,
  output out_25,
  output out_26
);

  wire adder_1_cout, adder_2_cout, adder_3_cout, adder_4_cout, adder_5_cout, adder_6_cout, adder_7_cout;

  Adder #(.width(1)) adder_1 (.a(in_2), .b(in_3), .out(out_18), .cin(in_1), .cout(adder_1_cout));
  Adder #(.width(1)) adder_2 (.a(in_4), .b(in_5), .out(out_19), .cin(adder_1_cout), .cout(adder_2_cout));
  Adder #(.width(1)) adder_3 (.a(in_6), .b(in_7), .out(out_20), .cin(adder_2_cout), .cout(adder_3_cout));
  Adder #(.width(1)) adder_4 (.a(in_8), .b(in_9), .out(out_21), .cin(adder_3_cout), .cout(adder_4_cout));
  Adder #(.width(1)) adder_5 (.a(in_10), .b(in_11), .out(out_22), .cin(adder_4_cout), .cout(adder_5_cout));
  Adder #(.width(1)) adder_6 (.a(in_12), .b(in_13), .out(out_23), .cin(adder_5_cout), .cout(adder_6_cout));
  Adder #(.width(1)) adder_7 (.a(in_14), .b(in_15), .out(out_24), .cin(adder_6_cout), .cout(adder_7_cout));
  Adder #(.width(1)) adder_8 (.a(in_16), .b(in_17), .out(out_25), .cin(adder_7_cout), .cout(out_26));

  // Notes on the sheet:
  //   8-BIT ADDER
endmodule

// 10 BY 8 BIT MULTIPLLIER
module Multiplier (
  input  in_1,
  input  in_2,
  input  in_3,
  input  in_4,
  input  in_5,
  input  in_6,
  input  in_7,
  input  in_8,
  input  in_9,
  input  in_10,
  input  in_11,
  input  in_12,
  input  in_13,
  input  in_14,
  input  in_15,
  input  in_16,
  input  in_17,
  input  in_18,
  output out_19,
  output out_20,
  output out_21,
  output out_22,
  output out_23,
  output out_24,
  output out_25,
  output out_26,
  output out_27,
  output out_28,
  output out_29,
  output out_30,
  output out_31,
  output out_32,
  output out_33,
  output out_34,
  output out_35,
  output out_36
);

  wire and_1_out, and_2_out, and_3_out, and_4_out, and_5_out, and_6_out, and_7_out, and_8_out, and_9_out,
       and_10_out, and_11_out, and_12_out, and_13_out, and_14_out, and_15_out, and_16_out, and_17_out,
       and_18_out, and_19_out, and_20_out, and_21_out, and_22_out, and_23_out, and_24_out, and_25_out,
       and_26_out, and_27_out, and_28_out, and_29_out, and_30_out, and_31_out, and_32_out, and_33_out,
       and_34_out, and_35_out, and_36_out, and_37_out, and_38_out, and_39_out, and_40_out, and_41_out,
       and_42_out, and_43_out, and_44_out, and_45_out, and_46_out, and_47_out, and_48_out, and_49_out,
       and_50_out, and_51_out, and_52_out, and_53_out, and_54_out, and_55_out, and_56_out, and_57_out,
       and_58_out, and_59_out, and_60_out, and_61_out, and_62_out, and_63_out, and_64_out, and_65_out,
       and_66_out, and_67_out, and_68_out, and_69_out, and_70_out, and_71_out, and_72_out, and_73_out,
       and_74_out, and_75_out, and_76_out, and_77_out, and_78_out, and_79_out, n8_bit_adder_1_out_19,
       n8_bit_adder_1_out_20, n8_bit_adder_1_out_21, n8_bit_adder_1_out_22, n8_bit_adder_1_out_23,
       n8_bit_adder_1_out_24, n8_bit_adder_1_out_25, n8_bit_adder_1_out_26, n8_bit_adder_3_out_19,
       n8_bit_adder_3_out_20, n8_bit_adder_3_out_21, n8_bit_adder_3_out_22, n8_bit_adder_3_out_23,
       n8_bit_adder_3_out_24, n8_bit_adder_3_out_25, n8_bit_adder_3_out_26, n8_bit_adder_4_out_19,
       n8_bit_adder_4_out_20, n8_bit_adder_4_out_21, n8_bit_adder_4_out_22, n8_bit_adder_4_out_23,
       n8_bit_adder_4_out_24, n8_bit_adder_4_out_25, n8_bit_adder_4_out_26, n8_bit_adder_5_out_19,
       n8_bit_adder_5_out_20, n8_bit_adder_5_out_21, n8_bit_adder_5_out_22, n8_bit_adder_5_out_23,
       n8_bit_adder_5_out_24, n8_bit_adder_5_out_25, n8_bit_adder_5_out_26, n8_bit_adder_6_out_19,
       n8_bit_adder_6_out_20, n8_bit_adder_6_out_21, n8_bit_adder_6_out_22, n8_bit_adder_6_out_23,
       n8_bit_adder_6_out_24, n8_bit_adder_6_out_25, n8_bit_adder_6_out_26, n8_bit_adder_7_out_19,
       n8_bit_adder_7_out_20, n8_bit_adder_7_out_21, n8_bit_adder_7_out_22, n8_bit_adder_7_out_23,
       n8_bit_adder_7_out_24, n8_bit_adder_7_out_25, n8_bit_adder_7_out_26, n8_bit_adder_8_out_19,
       n8_bit_adder_8_out_20, n8_bit_adder_8_out_21, n8_bit_adder_8_out_22, n8_bit_adder_8_out_23,
       n8_bit_adder_8_out_24, n8_bit_adder_8_out_25, n8_bit_adder_8_out_26, n8_bit_adder_9_out_19,
       n8_bit_adder_9_out_20, n8_bit_adder_9_out_21, n8_bit_adder_9_out_22, n8_bit_adder_9_out_23,
       n8_bit_adder_9_out_24, n8_bit_adder_9_out_25, n8_bit_adder_9_out_26;

  and and_1 (and_1_out, in_11, in_1);
  and and_2 (and_2_out, in_11, in_2);
  and and_3 (and_3_out, in_12, in_1);
  and and_4 (and_4_out, in_11, in_4);
  and and_5 (and_5_out, in_11, in_3);
  and and_6 (and_6_out, in_12, in_3);
  and and_7 (and_7_out, in_12, in_2);
  and and_8 (and_8_out, in_13, in_2);
  and and_9 (and_9_out, in_13, in_1);
  and and_10 (and_10_out, in_11, in_5);
  and and_11 (and_11_out, in_12, in_4);
  and and_12 (and_12_out, in_13, in_3);
  and and_13 (and_13_out, in_14, in_2);
  and and_14 (and_14_out, in_15, in_1);
  and and_15 (and_15_out, in_14, in_1);
  and and_16 (and_16_out, in_11, in_8);
  and and_17 (and_17_out, in_12, in_8);
  and and_18 (and_18_out, in_11, in_7);
  and and_19 (and_19_out, in_12, in_7);
  and and_20 (and_20_out, in_11, in_6);
  and and_21 (and_21_out, in_12, in_5);
  and and_22 (and_22_out, in_14, in_4);
  and and_23 (and_23_out, in_13, in_4);
  and and_24 (and_24_out, in_14, in_3);
  and and_25 (and_25_out, in_15, in_2);
  and and_26 (and_26_out, in_16, in_1);
  and and_27 (and_27_out, in_13, in_8);
  and and_28 (and_28_out, in_13, in_7);
  and and_29 (and_29_out, in_13, in_6);
  and and_30 (and_30_out, in_12, in_6);
  and and_31 (and_31_out, in_13, in_5);
  and and_32 (and_32_out, in_14, in_5);
  and and_33 (and_33_out, in_15, in_4);
  and and_34 (and_34_out, in_15, in_3);
  and and_35 (and_35_out, in_16, in_3);
  and and_36 (and_36_out, in_17, in_2);
  and and_37 (and_37_out, in_16, in_2);
  and and_38 (and_38_out, in_17, in_1);
  and and_39 (and_39_out, in_11, in_9);
  and and_40 (and_40_out, in_14, in_8);
  and and_41 (and_41_out, in_14, in_7);
  and and_42 (and_42_out, in_14, in_6);
  and and_43 (and_43_out, in_15, in_5);
  and and_44 (and_44_out, in_16, in_4);
  and and_45 (and_45_out, in_17, in_3);
  and and_46 (and_46_out, in_18, in_2);
  and and_47 (and_47_out, in_18, in_1);
  and and_48 (and_48_out, in_12, in_9);
  and and_49 (and_49_out, in_13, in_9);
  and and_50 (and_50_out, in_16, in_8);
  and and_51 (and_51_out, in_15, in_8);
  and and_52 (and_52_out, in_16, in_7);
  and and_53 (and_53_out, in_15, in_7);
  and and_54 (and_54_out, in_15, in_6);
  and and_55 (and_55_out, in_16, in_5);
  and and_56 (and_56_out, in_17, in_4);
  and and_57 (and_57_out, in_18, in_4);
  and and_58 (and_58_out, in_18, in_3);
  and and_59 (and_59_out, in_14, in_9);
  and and_60 (and_60_out, in_17, in_8);
  and and_61 (and_61_out, in_17, in_7);
  and and_62 (and_62_out, in_17, in_6);
  and and_63 (and_63_out, in_16, in_6);
  and and_64 (and_64_out, in_18, in_5);
  and and_65 (and_65_out, in_17, in_5);
  and and_66 (and_66_out, in_15, in_9);
  and and_67 (and_67_out, in_18, in_8);
  and and_68 (and_68_out, in_18, in_7);
  and and_69 (and_69_out, in_18, in_6);
  and and_70 (and_70_out, in_17, in_9);
  and and_71 (and_71_out, in_16, in_9);
  and and_72 (and_72_out, in_18, in_9);
  _8_bit_adder u_8_bit_adder_1 (
    .in_2(n8_bit_adder_3_out_19), .in_3(and_46_out), .in_4(n8_bit_adder_3_out_20), .in_5(and_36_out),
    .in_6(n8_bit_adder_3_out_21), .in_7(and_37_out), .in_8(n8_bit_adder_3_out_22), .in_9(and_25_out),
    .in_10(n8_bit_adder_3_out_23), .in_11(and_13_out), .in_12(n8_bit_adder_3_out_24), .in_13(and_8_out),
    .in_14(n8_bit_adder_3_out_25), .in_15(and_7_out), .in_16(n8_bit_adder_3_out_26), .in_17(and_2_out),
    .out_18(out_28), .out_19(n8_bit_adder_1_out_19), .out_20(n8_bit_adder_1_out_20),
    .out_21(n8_bit_adder_1_out_21), .out_22(n8_bit_adder_1_out_22), .out_23(n8_bit_adder_1_out_23),
    .out_24(n8_bit_adder_1_out_24), .out_25(n8_bit_adder_1_out_25), .out_26(n8_bit_adder_1_out_26));  // open: in_1
  _8_bit_adder u_8_bit_adder_2 (
    .in_2(n8_bit_adder_1_out_19), .in_3(and_47_out), .in_4(n8_bit_adder_1_out_20), .in_5(and_38_out),
    .in_6(n8_bit_adder_1_out_21), .in_7(and_26_out), .in_8(n8_bit_adder_1_out_22), .in_9(and_14_out),
    .in_10(n8_bit_adder_1_out_23), .in_11(and_15_out), .in_12(n8_bit_adder_1_out_24), .in_13(and_9_out),
    .in_14(n8_bit_adder_1_out_25), .in_15(and_3_out), .in_16(n8_bit_adder_1_out_26), .in_17(and_1_out),
    .out_18(out_27), .out_19(out_26), .out_20(out_25), .out_21(out_24), .out_22(out_23), .out_23(out_22),
    .out_24(out_21), .out_25(out_20), .out_26(out_19));  // open: in_1
  and and_73 (and_73_out, in_11, in_10);
  _8_bit_adder u_8_bit_adder_3 (
    .in_2(n8_bit_adder_5_out_19), .in_3(and_58_out), .in_4(n8_bit_adder_5_out_20), .in_5(and_45_out),
    .in_6(n8_bit_adder_5_out_21), .in_7(and_35_out), .in_8(n8_bit_adder_5_out_22), .in_9(and_34_out),
    .in_10(n8_bit_adder_5_out_23), .in_11(and_24_out), .in_12(n8_bit_adder_5_out_24), .in_13(and_12_out),
    .in_14(n8_bit_adder_5_out_25), .in_15(and_6_out), .in_16(n8_bit_adder_5_out_26), .in_17(and_5_out),
    .out_18(out_29), .out_19(n8_bit_adder_3_out_19), .out_20(n8_bit_adder_3_out_20),
    .out_21(n8_bit_adder_3_out_21), .out_22(n8_bit_adder_3_out_22), .out_23(n8_bit_adder_3_out_23),
    .out_24(n8_bit_adder_3_out_24), .out_25(n8_bit_adder_3_out_25), .in_1(1'b0),
    .out_26(n8_bit_adder_3_out_26));
  and and_74 (and_74_out, in_12, in_10);
  _8_bit_adder u_8_bit_adder_4 (
    .in_2(n8_bit_adder_7_out_19), .in_3(and_64_out), .in_4(n8_bit_adder_7_out_20), .in_5(and_65_out),
    .in_6(n8_bit_adder_7_out_21), .in_7(and_55_out), .in_8(n8_bit_adder_7_out_22), .in_9(and_43_out),
    .in_10(n8_bit_adder_7_out_23), .in_11(and_32_out), .in_12(n8_bit_adder_7_out_24), .in_13(and_31_out),
    .in_14(n8_bit_adder_7_out_25), .in_15(and_21_out), .in_16(n8_bit_adder_7_out_26), .in_17(and_10_out),
    .out_18(out_31), .out_19(n8_bit_adder_4_out_19), .out_20(n8_bit_adder_4_out_20),
    .out_21(n8_bit_adder_4_out_21), .out_22(n8_bit_adder_4_out_22), .out_23(n8_bit_adder_4_out_23),
    .out_24(n8_bit_adder_4_out_24), .out_25(n8_bit_adder_4_out_25), .in_1(1'b0),
    .out_26(n8_bit_adder_4_out_26));
  _8_bit_adder u_8_bit_adder_5 (
    .in_2(n8_bit_adder_4_out_19), .in_3(and_57_out), .in_4(n8_bit_adder_4_out_20), .in_5(and_56_out),
    .in_6(n8_bit_adder_4_out_21), .in_7(and_44_out), .in_8(n8_bit_adder_4_out_22), .in_9(and_33_out),
    .in_10(n8_bit_adder_4_out_23), .in_11(and_22_out), .in_12(n8_bit_adder_4_out_24), .in_13(and_23_out),
    .in_14(n8_bit_adder_4_out_25), .in_15(and_11_out), .in_16(n8_bit_adder_4_out_26), .in_17(and_4_out),
    .out_18(out_30), .out_19(n8_bit_adder_5_out_19), .out_20(n8_bit_adder_5_out_20),
    .out_21(n8_bit_adder_5_out_21), .out_22(n8_bit_adder_5_out_22), .out_23(n8_bit_adder_5_out_23),
    .out_24(n8_bit_adder_5_out_24), .out_25(n8_bit_adder_5_out_25), .in_1(1'b0),
    .out_26(n8_bit_adder_5_out_26));
  and and_75 (and_75_out, in_13, in_10);
  _8_bit_adder u_8_bit_adder_6 (
    .in_2(n8_bit_adder_8_out_19), .in_3(and_68_out), .in_4(n8_bit_adder_8_out_20), .in_5(and_61_out),
    .in_6(n8_bit_adder_8_out_21), .in_7(and_52_out), .in_8(n8_bit_adder_8_out_22), .in_9(and_53_out),
    .in_10(n8_bit_adder_8_out_23), .in_11(and_41_out), .in_12(n8_bit_adder_8_out_24), .in_13(and_28_out),
    .in_14(n8_bit_adder_8_out_25), .in_15(and_19_out), .in_16(n8_bit_adder_8_out_26), .in_17(and_18_out),
    .out_18(out_33), .out_19(n8_bit_adder_6_out_19), .out_20(n8_bit_adder_6_out_20),
    .out_21(n8_bit_adder_6_out_21), .out_22(n8_bit_adder_6_out_22), .out_23(n8_bit_adder_6_out_23),
    .out_24(n8_bit_adder_6_out_24), .out_25(n8_bit_adder_6_out_25), .in_1(1'b0),
    .out_26(n8_bit_adder_6_out_26));
  _8_bit_adder u_8_bit_adder_7 (
    .in_2(n8_bit_adder_6_out_19), .in_3(and_69_out), .in_4(n8_bit_adder_6_out_20), .in_5(and_62_out),
    .in_6(n8_bit_adder_6_out_21), .in_7(and_63_out), .in_8(n8_bit_adder_6_out_22), .in_9(and_54_out),
    .in_10(n8_bit_adder_6_out_23), .in_11(and_42_out), .in_12(n8_bit_adder_6_out_24), .in_13(and_29_out),
    .in_14(n8_bit_adder_6_out_25), .in_15(and_30_out), .in_16(n8_bit_adder_6_out_26), .in_17(and_20_out),
    .out_18(out_32), .out_19(n8_bit_adder_7_out_19), .out_20(n8_bit_adder_7_out_20),
    .out_21(n8_bit_adder_7_out_21), .out_22(n8_bit_adder_7_out_22), .out_23(n8_bit_adder_7_out_23),
    .out_24(n8_bit_adder_7_out_24), .out_25(n8_bit_adder_7_out_25), .in_1(1'b0),
    .out_26(n8_bit_adder_7_out_26));
  and and_76 (and_76_out, in_14, in_10);
  and and_77 (and_77_out, in_15, in_10);
  _8_bit_adder u_8_bit_adder_8 (
    .in_2(n8_bit_adder_9_out_19), .in_3(and_67_out), .in_4(n8_bit_adder_9_out_20), .in_5(and_60_out),
    .in_6(n8_bit_adder_9_out_21), .in_7(and_50_out), .in_8(n8_bit_adder_9_out_22), .in_9(and_51_out),
    .in_10(n8_bit_adder_9_out_23), .in_11(and_40_out), .in_12(n8_bit_adder_9_out_24), .in_13(and_27_out),
    .in_14(n8_bit_adder_9_out_25), .in_15(and_17_out), .in_16(n8_bit_adder_9_out_26), .in_17(and_16_out),
    .out_18(out_34), .out_19(n8_bit_adder_8_out_19), .out_20(n8_bit_adder_8_out_20),
    .out_21(n8_bit_adder_8_out_21), .out_22(n8_bit_adder_8_out_22), .out_23(n8_bit_adder_8_out_23),
    .out_24(n8_bit_adder_8_out_24), .out_25(n8_bit_adder_8_out_25), .in_1(1'b0),
    .out_26(n8_bit_adder_8_out_26));
  and and_78 (and_78_out, in_16, in_10);
  _8_bit_adder u_8_bit_adder_9 (
    .in_2(and_79_out), .in_3(and_72_out), .in_4(and_78_out), .in_5(and_70_out), .in_6(and_77_out),
    .in_7(and_71_out), .in_8(and_76_out), .in_9(and_66_out), .in_10(and_75_out), .in_11(and_59_out),
    .in_12(and_74_out), .in_13(and_49_out), .in_14(and_73_out), .in_15(and_48_out), .in_16(1'b0),
    .in_17(and_39_out), .out_18(out_35), .out_19(n8_bit_adder_9_out_19), .out_20(n8_bit_adder_9_out_20),
    .out_21(n8_bit_adder_9_out_21), .out_22(n8_bit_adder_9_out_22), .out_23(n8_bit_adder_9_out_23),
    .out_24(n8_bit_adder_9_out_24), .out_25(n8_bit_adder_9_out_25), .in_1(1'b0),
    .out_26(n8_bit_adder_9_out_26));
  and and_79 (and_79_out, in_17, in_10);
  and and_80 (out_36, in_18, in_10);

  // Other names for the same wires on the sheet: A0 = in_10; A1 = in_9; A2 = in_8; A3 = in_7; A4 = in_6; A5 = in_5;
  //   A6 = in_4; A7 = in_3; A8 = in_2; A9 = in_1; B0 = in_18; B1 = in_17; B2 = in_16; B3 = in_15; B4 = in_14;
  //   B5 = in_13; B6 = in_12; B7 = in_11

  // Notes on the sheet:
  //   10 BY 8 BIT MULTIPLIER
endmodule

// DIVISION CIRCUIT
module Divider (
  input  in_1,
  input  in_2,
  input  in_3,
  input  in_4,
  input  in_5,
  input  in_6,
  input  in_7,
  input  in_8,
  input  in_9,
  input  in_10,
  input  in_11,
  input  in_12,
  input  in_13,
  input  in_14,
  output [7:0] QUOTIENT,
  output [6:0] REMAINDER
);

  wire processing_unit_2_cout, processing_unit_2_muxoutput, processing_unit_4_cout,
       processing_unit_4_muxoutput, processing_unit_5_cout, processing_unit_5_muxoutput,
       processing_unit_7_cout, processing_unit_7_muxoutput, processing_unit_8_cout,
       processing_unit_8_muxoutput, processing_unit_9_cout, processing_unit_9_muxoutput,
       processing_unit_11_cout, processing_unit_11_muxoutput, processing_unit_12_cout,
       processing_unit_12_muxoutput, processing_unit_13_cout, processing_unit_13_muxoutput,
       processing_unit_14_cout, processing_unit_14_muxoutput, processing_unit_16_cout,
       processing_unit_16_muxoutput, processing_unit_17_cout, processing_unit_17_muxoutput,
       processing_unit_18_cout, processing_unit_18_muxoutput, processing_unit_19_cout,
       processing_unit_19_muxoutput, processing_unit_20_cout, processing_unit_20_muxoutput,
       processing_unit_21_muxoutput, processing_unit_23_cout, processing_unit_23_muxoutput,
       processing_unit_24_cout, processing_unit_24_muxoutput, processing_unit_25_cout,
       processing_unit_25_muxoutput, processing_unit_26_cout, processing_unit_26_muxoutput,
       processing_unit_27_cout, processing_unit_27_muxoutput, processing_unit_28_cout,
       processing_unit_28_muxoutput, processing_unit_30_cout, processing_unit_30_muxoutput,
       processing_unit_31_cout, processing_unit_31_muxoutput, processing_unit_32_cout,
       processing_unit_32_muxoutput, processing_unit_33_cout, processing_unit_33_muxoutput,
       processing_unit_34_cout, processing_unit_34_muxoutput, processing_unit_35_cout,
       processing_unit_36_cout, processing_unit_36_muxoutput, processing_unit_37_cout,
       processing_unit_37_muxoutput, processing_unit_38_cout, processing_unit_38_muxoutput,
       processing_unit_39_cout, processing_unit_39_muxoutput, processing_unit_40_cout,
       processing_unit_41_cout, processing_unit_41_muxoutput, processing_unit_42_cout,
       processing_unit_42_muxoutput, processing_unit_43_cout, processing_unit_43_muxoutput,
       processing_unit_44_cout, processing_unit_45_cout, processing_unit_45_muxoutput,
       processing_unit_46_cout, processing_unit_46_muxoutput, processing_unit_47_cout,
       processing_unit_48_cout, processing_unit_48_muxoutput, processing_unit_49_cout,
       processing_unit_50_cout;

  Processing_Unit processing_unit_1 (
    .D(1'b0), .d_2(in_1), .CIN(processing_unit_2_cout), .COUT(QUOTIENT[7]), .SELECT_LINE(QUOTIENT[7]));  // open: muxOutput
  Processing_Unit processing_unit_2 (
    .D(1'b0), .d_2(in_2), .muxOutput(processing_unit_2_muxoutput), .CIN(processing_unit_4_cout),
    .COUT(processing_unit_2_cout), .SELECT_LINE(QUOTIENT[7]));
  Processing_Unit processing_unit_3 (
    .D(processing_unit_2_muxoutput), .d_2(in_1), .CIN(processing_unit_5_cout), .COUT(QUOTIENT[6]),
    .SELECT_LINE(QUOTIENT[6]));  // open: muxOutput
  Processing_Unit processing_unit_4 (
    .D(1'b0), .d_2(in_3), .muxOutput(processing_unit_4_muxoutput), .CIN(processing_unit_7_cout),
    .COUT(processing_unit_4_cout), .SELECT_LINE(QUOTIENT[7]));
  Processing_Unit processing_unit_5 (
    .D(processing_unit_4_muxoutput), .d_2(in_2), .muxOutput(processing_unit_5_muxoutput),
    .CIN(processing_unit_8_cout), .COUT(processing_unit_5_cout), .SELECT_LINE(QUOTIENT[6]));
  Processing_Unit processing_unit_6 (
    .D(processing_unit_5_muxoutput), .d_2(in_1), .CIN(processing_unit_9_cout), .COUT(QUOTIENT[5]),
    .SELECT_LINE(QUOTIENT[5]));  // open: muxOutput
  Processing_Unit processing_unit_7 (
    .D(1'b0), .d_2(in_4), .muxOutput(processing_unit_7_muxoutput), .CIN(processing_unit_11_cout),
    .COUT(processing_unit_7_cout), .SELECT_LINE(QUOTIENT[7]));
  Processing_Unit processing_unit_8 (
    .D(processing_unit_7_muxoutput), .d_2(in_3), .muxOutput(processing_unit_8_muxoutput),
    .CIN(processing_unit_12_cout), .COUT(processing_unit_8_cout), .SELECT_LINE(QUOTIENT[6]));
  Processing_Unit processing_unit_9 (
    .D(processing_unit_8_muxoutput), .d_2(in_2), .muxOutput(processing_unit_9_muxoutput),
    .CIN(processing_unit_13_cout), .COUT(processing_unit_9_cout), .SELECT_LINE(QUOTIENT[5]));
  Processing_Unit processing_unit_10 (
    .D(processing_unit_9_muxoutput), .d_2(in_1), .CIN(processing_unit_14_cout), .COUT(QUOTIENT[4]),
    .SELECT_LINE(QUOTIENT[4]));  // open: muxOutput
  Processing_Unit processing_unit_11 (
    .D(1'b0), .d_2(in_5), .muxOutput(processing_unit_11_muxoutput), .CIN(processing_unit_16_cout),
    .COUT(processing_unit_11_cout), .SELECT_LINE(QUOTIENT[7]));
  Processing_Unit processing_unit_12 (
    .D(processing_unit_11_muxoutput), .d_2(in_4), .muxOutput(processing_unit_12_muxoutput),
    .CIN(processing_unit_17_cout), .COUT(processing_unit_12_cout), .SELECT_LINE(QUOTIENT[6]));
  Processing_Unit processing_unit_13 (
    .D(processing_unit_12_muxoutput), .d_2(in_3), .muxOutput(processing_unit_13_muxoutput),
    .CIN(processing_unit_18_cout), .COUT(processing_unit_13_cout), .SELECT_LINE(QUOTIENT[5]));
  Processing_Unit processing_unit_14 (
    .D(processing_unit_13_muxoutput), .d_2(in_2), .muxOutput(processing_unit_14_muxoutput),
    .CIN(processing_unit_19_cout), .COUT(processing_unit_14_cout), .SELECT_LINE(QUOTIENT[4]));
  Processing_Unit processing_unit_15 (
    .D(processing_unit_14_muxoutput), .d_2(in_1), .CIN(processing_unit_20_cout), .COUT(QUOTIENT[3]),
    .SELECT_LINE(QUOTIENT[3]));  // open: muxOutput
  Processing_Unit processing_unit_16 (
    .D(in_7), .d_2(in_6), .muxOutput(processing_unit_16_muxoutput), .CIN(1'b1),
    .COUT(processing_unit_16_cout), .SELECT_LINE(QUOTIENT[7]));
  Processing_Unit processing_unit_17 (
    .D(processing_unit_16_muxoutput), .d_2(in_5), .muxOutput(processing_unit_17_muxoutput),
    .CIN(processing_unit_23_cout), .COUT(processing_unit_17_cout), .SELECT_LINE(QUOTIENT[6]));
  Processing_Unit processing_unit_18 (
    .D(processing_unit_17_muxoutput), .d_2(in_4), .muxOutput(processing_unit_18_muxoutput),
    .CIN(processing_unit_24_cout), .COUT(processing_unit_18_cout), .SELECT_LINE(QUOTIENT[5]));
  Processing_Unit processing_unit_19 (
    .D(processing_unit_18_muxoutput), .d_2(in_3), .muxOutput(processing_unit_19_muxoutput),
    .CIN(processing_unit_25_cout), .COUT(processing_unit_19_cout), .SELECT_LINE(QUOTIENT[4]));
  Processing_Unit processing_unit_20 (
    .D(processing_unit_19_muxoutput), .d_2(in_2), .muxOutput(processing_unit_20_muxoutput),
    .CIN(processing_unit_26_cout), .COUT(processing_unit_20_cout), .SELECT_LINE(QUOTIENT[3]));
  Processing_Unit processing_unit_21 (
    .D(processing_unit_20_muxoutput), .d_2(in_1), .muxOutput(processing_unit_21_muxoutput),
    .CIN(processing_unit_27_cout), .COUT(QUOTIENT[2]), .SELECT_LINE(QUOTIENT[2]));
  Processing_Unit processing_unit_22 (
    .D(processing_unit_21_muxoutput), .d_2(1'b0), .CIN(processing_unit_28_cout), .COUT(QUOTIENT[1]),
    .SELECT_LINE(QUOTIENT[1]));  // open: muxOutput
  Processing_Unit processing_unit_23 (
    .D(in_8), .d_2(in_6), .muxOutput(processing_unit_23_muxoutput), .CIN(1'b1),
    .COUT(processing_unit_23_cout), .SELECT_LINE(QUOTIENT[6]));
  Processing_Unit processing_unit_24 (
    .D(processing_unit_23_muxoutput), .d_2(in_5), .muxOutput(processing_unit_24_muxoutput),
    .CIN(processing_unit_30_cout), .COUT(processing_unit_24_cout), .SELECT_LINE(QUOTIENT[5]));
  Processing_Unit processing_unit_25 (
    .D(processing_unit_24_muxoutput), .d_2(in_4), .muxOutput(processing_unit_25_muxoutput),
    .CIN(processing_unit_31_cout), .COUT(processing_unit_25_cout), .SELECT_LINE(QUOTIENT[4]));
  Processing_Unit processing_unit_26 (
    .D(processing_unit_25_muxoutput), .d_2(in_3), .muxOutput(processing_unit_26_muxoutput),
    .CIN(processing_unit_32_cout), .COUT(processing_unit_26_cout), .SELECT_LINE(QUOTIENT[3]));
  Processing_Unit processing_unit_27 (
    .D(processing_unit_26_muxoutput), .d_2(in_2), .muxOutput(processing_unit_27_muxoutput),
    .CIN(processing_unit_33_cout), .COUT(processing_unit_27_cout), .SELECT_LINE(QUOTIENT[2]));
  Processing_Unit processing_unit_28 (
    .D(processing_unit_27_muxoutput), .d_2(in_1), .muxOutput(processing_unit_28_muxoutput),
    .CIN(processing_unit_34_cout), .COUT(processing_unit_28_cout), .SELECT_LINE(QUOTIENT[1]));
  Processing_Unit processing_unit_29 (
    .D(processing_unit_28_muxoutput), .d_2(1'b0), .muxOutput(REMAINDER[6]), .CIN(processing_unit_35_cout),
    .COUT(QUOTIENT[0]), .SELECT_LINE(QUOTIENT[0]));
  Processing_Unit processing_unit_30 (
    .D(in_9), .d_2(in_6), .muxOutput(processing_unit_30_muxoutput), .CIN(1'b1),
    .COUT(processing_unit_30_cout), .SELECT_LINE(QUOTIENT[5]));
  Processing_Unit processing_unit_31 (
    .D(processing_unit_30_muxoutput), .d_2(in_5), .muxOutput(processing_unit_31_muxoutput),
    .CIN(processing_unit_36_cout), .COUT(processing_unit_31_cout), .SELECT_LINE(QUOTIENT[4]));
  Processing_Unit processing_unit_32 (
    .D(processing_unit_31_muxoutput), .d_2(in_4), .muxOutput(processing_unit_32_muxoutput),
    .CIN(processing_unit_37_cout), .COUT(processing_unit_32_cout), .SELECT_LINE(QUOTIENT[3]));
  Processing_Unit processing_unit_33 (
    .D(processing_unit_32_muxoutput), .d_2(in_3), .muxOutput(processing_unit_33_muxoutput),
    .CIN(processing_unit_38_cout), .COUT(processing_unit_33_cout), .SELECT_LINE(QUOTIENT[2]));
  Processing_Unit processing_unit_34 (
    .D(processing_unit_33_muxoutput), .d_2(in_2), .muxOutput(processing_unit_34_muxoutput),
    .CIN(processing_unit_39_cout), .COUT(processing_unit_34_cout), .SELECT_LINE(QUOTIENT[1]));
  Processing_Unit processing_unit_35 (
    .D(processing_unit_34_muxoutput), .d_2(in_1), .muxOutput(REMAINDER[5]), .CIN(processing_unit_40_cout),
    .COUT(processing_unit_35_cout), .SELECT_LINE(QUOTIENT[0]));
  Processing_Unit processing_unit_36 (
    .D(in_10), .d_2(in_6), .muxOutput(processing_unit_36_muxoutput), .CIN(1'b1),
    .COUT(processing_unit_36_cout), .SELECT_LINE(QUOTIENT[4]));
  Processing_Unit processing_unit_37 (
    .D(processing_unit_36_muxoutput), .d_2(in_5), .muxOutput(processing_unit_37_muxoutput),
    .CIN(processing_unit_41_cout), .COUT(processing_unit_37_cout), .SELECT_LINE(QUOTIENT[3]));
  Processing_Unit processing_unit_38 (
    .D(processing_unit_37_muxoutput), .d_2(in_4), .muxOutput(processing_unit_38_muxoutput),
    .CIN(processing_unit_42_cout), .COUT(processing_unit_38_cout), .SELECT_LINE(QUOTIENT[2]));
  Processing_Unit processing_unit_39 (
    .D(processing_unit_38_muxoutput), .d_2(in_3), .muxOutput(processing_unit_39_muxoutput),
    .CIN(processing_unit_43_cout), .COUT(processing_unit_39_cout), .SELECT_LINE(QUOTIENT[1]));
  Processing_Unit processing_unit_40 (
    .D(processing_unit_39_muxoutput), .d_2(in_2), .muxOutput(REMAINDER[4]), .CIN(processing_unit_44_cout),
    .COUT(processing_unit_40_cout), .SELECT_LINE(QUOTIENT[0]));
  Processing_Unit processing_unit_41 (
    .D(in_11), .d_2(in_6), .muxOutput(processing_unit_41_muxoutput), .CIN(1'b1),
    .COUT(processing_unit_41_cout), .SELECT_LINE(QUOTIENT[3]));
  Processing_Unit processing_unit_42 (
    .D(processing_unit_41_muxoutput), .d_2(in_5), .muxOutput(processing_unit_42_muxoutput),
    .CIN(processing_unit_45_cout), .COUT(processing_unit_42_cout), .SELECT_LINE(QUOTIENT[2]));
  Processing_Unit processing_unit_43 (
    .D(processing_unit_42_muxoutput), .d_2(in_4), .muxOutput(processing_unit_43_muxoutput),
    .CIN(processing_unit_46_cout), .COUT(processing_unit_43_cout), .SELECT_LINE(QUOTIENT[1]));
  Processing_Unit processing_unit_44 (
    .D(processing_unit_43_muxoutput), .d_2(in_3), .muxOutput(REMAINDER[3]), .CIN(processing_unit_47_cout),
    .COUT(processing_unit_44_cout), .SELECT_LINE(QUOTIENT[0]));
  Processing_Unit processing_unit_45 (
    .D(in_12), .d_2(in_6), .muxOutput(processing_unit_45_muxoutput), .CIN(1'b1),
    .COUT(processing_unit_45_cout), .SELECT_LINE(QUOTIENT[2]));
  Processing_Unit processing_unit_46 (
    .D(processing_unit_45_muxoutput), .d_2(in_5), .muxOutput(processing_unit_46_muxoutput),
    .CIN(processing_unit_48_cout), .COUT(processing_unit_46_cout), .SELECT_LINE(QUOTIENT[1]));
  Processing_Unit processing_unit_47 (
    .D(processing_unit_46_muxoutput), .d_2(in_4), .muxOutput(REMAINDER[2]), .CIN(processing_unit_49_cout),
    .COUT(processing_unit_47_cout), .SELECT_LINE(QUOTIENT[0]));
  Processing_Unit processing_unit_48 (
    .D(in_13), .d_2(in_6), .muxOutput(processing_unit_48_muxoutput), .CIN(1'b1),
    .COUT(processing_unit_48_cout), .SELECT_LINE(QUOTIENT[1]));
  Processing_Unit processing_unit_49 (
    .D(processing_unit_48_muxoutput), .d_2(in_5), .muxOutput(REMAINDER[1]), .CIN(processing_unit_50_cout),
    .COUT(processing_unit_49_cout), .SELECT_LINE(QUOTIENT[0]));
  Processing_Unit processing_unit_50 (
    .D(in_14), .d_2(in_6), .muxOutput(REMAINDER[0]), .CIN(1'b1), .COUT(processing_unit_50_cout),
    .SELECT_LINE(QUOTIENT[0]));

  // Other names for the same wires on the sheet: D0 = in_14; d0_t = in_6; D1 = in_13; d1_t = in_5; D2 = in_12;
  //   d2_t = in_4; D3 = in_11; d3_t = in_3; D4 = in_10; d4_t = in_2; D5 = in_9; d5_t = in_1; D6 = in_8; D7 = in_7

  // Notes on the sheet:
  //   which is decided by the Carry out of the last adder in the circuit which acts as the input to the select line of all the multiplexers in the current stage.
  //   Above is a 8 bit by 6 bit binary division circuit. The divisor is subtracted from the adequate number of bits of the dividend using two's complement method
  //   Each processing unit consists of a multiplexer which decides whether to send the subtracted value of the current computation to the stage of the circuit
  //   or to send the current dividend bits as it is to the next stage of the circuit depending upon whether the divisor is greater than or equal to the bits of the dividend
endmodule

// PROCESSOR
module Processing_Unit (
  input  CIN,
  input  D,
  input  d_2,
  input  SELECT_LINE,
  output muxOutput,
  output COUT
);

  wire adder_1_out, not_1_out;

  not not_1 (not_1_out, d_2);
  Adder #(.width(1)) adder_1 (.a(D), .b(not_1_out), .out(adder_1_out), .cin(CIN), .cout(COUT));
  Multiplexer multiplexer_1 (.in0(D), .in1(adder_1_out), .out(muxOutput), .sel(SELECT_LINE));  // open: en

  // Notes on the sheet:
  //   In this processing unit , the 2:1 multiplexer passes the dividend bit if select line is 0 and it passes the subtracted output if the select line is 1.
endmodule

// SEQUENTIAL
module SEQUENTIAL (
  input  in_1,
  input  ACTIVITY,
  input  in_3,
  input  RESET,
  output [2:0] ACTIVITY_2,
  output [5:0] SECONDS_RUN,
  output [5:0] SECONDS_WALK,
  output [5:0] SECONDS_CYCLE,
  output [5:0] TOTAL_TIME
);

  wire or_1_out;
  wire [5:0] register_1_q, subtractor_1_out;

  Register #(.width(6)) register_1 (.D(TOTAL_TIME), .Q(register_1_q), .clk(or_1_out));  // open: en, clr
  or or_1 (or_1_out, in_1, ACTIVITY, in_3);
  Clock clock_1 (
    .ACTIVITY(or_1_out), .RESET(RESET), .out_3(TOTAL_TIME[0]), .out_4(TOTAL_TIME[1]), .out_5(TOTAL_TIME[2]),
    .out_6(TOTAL_TIME[3]), .out_7(TOTAL_TIME[4]), .out_8(TOTAL_TIME[5]));
  Subtractor #(.width(6)) subtractor_1 (.a(TOTAL_TIME), .b(register_1_q), .out(subtractor_1_out));  // open: bin, bout
  Register #(.width(3)) register_2 (.D({in_3, ACTIVITY, in_1}), .en(1'b1), .Q(ACTIVITY_2), .clk(or_1_out), .clr(RESET));
  Register #(.width(6), .trigger("high")) register_3 (
    .D(subtractor_1_out), .en(1'b1), .Q(SECONDS_RUN), .clk(in_1), .clr(RESET));
  Register #(.width(6), .trigger("high")) register_4 (
    .D(subtractor_1_out), .en(1'b1), .Q(SECONDS_WALK), .clk(ACTIVITY), .clr(RESET));
  Register #(.width(6), .trigger("high")) register_5 (
    .D(subtractor_1_out), .en(1'b1), .Q(SECONDS_CYCLE), .clk(in_3), .clr(RESET));

  // Notes on the sheet:
  //   The ACTIVITY switches act as the start-stop button for the clock and the RESET button resets the counter to zero.
  //   Registers are used to store the values of the activity performed and the time elapsed while performing that activity.
  //   SEQUENTIAL COMPONENT OF THE GIVEN CIRCUIT
endmodule

module main (
  input  [6:0] RHR,
  input  [6:0] WEIGHT,
  input  [7:0] DISTANCE,
  input  CYCLE,
  input  WALK,
  input  RUN,
  input  RESET,
  output [17:0] CALORIE_RUN,
  output [17:0] CALORIE_WALK,
  output [17:0] CALORIE_CYCLE,
  output [7:0] THR,
  output [7:0] SPEED,
  output [6:0] ERROR_MARGIN
);

  wire [2:0] sequential_1_activity_2;
  wire [5:0] sequential_1_seconds_cycle, sequential_1_seconds_run, sequential_1_seconds_walk,
       sequential_1_total_time;
  wire [6:0] register_1_q, register_2_q;
  wire [7:0] register_3_q;

  Register #(.width(7), .trigger("low")) register_1 (.D(RHR), .en(1'b1), .Q(register_1_q), .clk(RESET), .clr(RESET));
  Heart_rate_Estimator heart_rate_estimator_1 (
    .TARGET_HR(THR), .RHR(register_1_q), .WEIGHT(register_2_q), .SPEED(SPEED));
  Register #(.width(7), .trigger("low")) register_2 (.D(WEIGHT), .en(1'b1), .Q(register_2_q), .clk(RESET), .clr(RESET));
  Speed_Calculator speed_calculator_1 (
    .TIME(sequential_1_total_time), .DISTANCE(register_3_q), .SPEED(SPEED), .REMAINDER_SPEED(ERROR_MARGIN));
  Register #(.trigger("low")) register_3 (.D(DISTANCE), .en(1'b1), .Q(register_3_q), .clk(RESET), .clr(RESET));
  Calorie_Counter calorie_counter_1 (
    .TIME(sequential_1_seconds_run), .ACTIVITY(sequential_1_activity_2), .WEIGHT(register_2_q),
    .CALORIES_BURNED(CALORIE_RUN));
  Calorie_Counter calorie_counter_2 (
    .TIME(sequential_1_seconds_walk), .ACTIVITY(sequential_1_activity_2), .WEIGHT(register_2_q),
    .CALORIES_BURNED(CALORIE_WALK));
  Calorie_Counter calorie_counter_3 (
    .TIME(sequential_1_seconds_cycle), .ACTIVITY(sequential_1_activity_2), .WEIGHT(register_2_q),
    .CALORIES_BURNED(CALORIE_CYCLE));
  SEQUENTIAL sequential_1 (
    .in_1(RUN), .ACTIVITY(WALK), .in_3(CYCLE), .RESET(RESET), .ACTIVITY_2(sequential_1_activity_2),
    .SECONDS_CYCLE(sequential_1_seconds_cycle), .SECONDS_RUN(sequential_1_seconds_run),
    .SECONDS_WALK(sequential_1_seconds_walk), .TOTAL_TIME(sequential_1_total_time));

  // Notes on the sheet:
  //   INSTRUCTIONS: 
  //   4) Make sure that at a time only one activity is toggled on 
  //   1) RESET buttion resets the circuit and allows us to enter the data such as Weight, Age, etc. of a new user
  //   3) Once an activity has been performed, set the activity switch as 0 to get the final data after performing the activity
  //   CHRONOFIT : FITNESS STOPWATCH
  //   OVERALL CIRCUIT
  //   2) The inputs of the activities are timed and depending upon the time the activity has been performed, the circuit provides us with real time, above given fitness data
  //   Team ID: S2 - T5
  //   Saksham Parmar, 231CS253
  //   Atharv Rajurkar, 231CS215
  //   Manish Agarwal, 231CS232
endmodule

// CALORIE CALCULATOR
module Calorie_Counter (
  input  [2:0] ACTIVITY,
  input  [5:0] TIME,
  input  [6:0] WEIGHT,
  output [17:0] CALORIES_BURNED
);

  wire and_1_out, and_2_out, and_3_out, multiplier_1_out_27, multiplier_1_out_28, multiplier_1_out_29,
       multiplier_1_out_30, multiplier_1_out_31, multiplier_1_out_32, multiplier_1_out_33,
       multiplier_1_out_34, multiplier_1_out_35, multiplier_1_out_36, not_1_out, not_2_out, not_3_out,
       or_1_out;

  not not_1 (not_1_out, ACTIVITY[2]);
  Multiplier multiplier_1 (
    .in_1(1'b0), .in_2(1'b0), .in_3(1'b0), .in_4(1'b0), .in_5(TIME[5]), .in_6(TIME[4]), .in_7(TIME[3]),
    .in_8(TIME[2]), .in_9(TIME[1]), .in_10(TIME[0]), .in_11(1'b0), .in_12(1'b0), .in_13(1'b0), .in_14(1'b0),
    .in_15(or_1_out), .in_16(and_3_out), .in_17(and_2_out), .in_18(and_3_out), .out_27(multiplier_1_out_27),
    .out_28(multiplier_1_out_28), .out_29(multiplier_1_out_29), .out_30(multiplier_1_out_30),
    .out_31(multiplier_1_out_31), .out_32(multiplier_1_out_32), .out_33(multiplier_1_out_33),
    .out_34(multiplier_1_out_34), .out_35(multiplier_1_out_35), .out_36(multiplier_1_out_36));  // open: out_19, out_20, out_21, out_22, out_23, out_24, out_25, out_26
  not not_2 (not_2_out, ACTIVITY[1]);
  and and_1 (and_1_out, not_1_out, not_2_out);
  or or_1 (or_1_out, and_1_out, and_2_out);
  not not_3 (not_3_out, ACTIVITY[0]);
  and and_2 (and_2_out, not_2_out, not_3_out);
  Multiplier multiplier_2 (
    .in_1(multiplier_1_out_27), .in_2(multiplier_1_out_28), .in_3(multiplier_1_out_29),
    .in_4(multiplier_1_out_30), .in_5(multiplier_1_out_31), .in_6(multiplier_1_out_32),
    .in_7(multiplier_1_out_33), .in_8(multiplier_1_out_34), .in_9(multiplier_1_out_35),
    .in_10(multiplier_1_out_36), .in_11(1'b0), .in_12(WEIGHT[6]), .in_13(WEIGHT[5]), .in_14(WEIGHT[4]),
    .in_15(WEIGHT[3]), .in_16(WEIGHT[2]), .in_17(WEIGHT[1]), .in_18(WEIGHT[0]), .out_19(CALORIES_BURNED[17]),
    .out_20(CALORIES_BURNED[16]), .out_21(CALORIES_BURNED[15]), .out_22(CALORIES_BURNED[14]),
    .out_23(CALORIES_BURNED[13]), .out_24(CALORIES_BURNED[12]), .out_25(CALORIES_BURNED[11]),
    .out_26(CALORIES_BURNED[10]), .out_27(CALORIES_BURNED[9]), .out_28(CALORIES_BURNED[8]),
    .out_29(CALORIES_BURNED[7]), .out_30(CALORIES_BURNED[6]), .out_31(CALORIES_BURNED[5]),
    .out_32(CALORIES_BURNED[4]), .out_33(CALORIES_BURNED[3]), .out_34(CALORIES_BURNED[2]),
    .out_35(CALORIES_BURNED[1]), .out_36(CALORIES_BURNED[0]));
  and and_3 (and_3_out, not_3_out, not_1_out);

  // Notes on the sheet:
  //   CALORIE CALCULATOR
  //   Calculates calories burned based on the formula: (MET of the activity) * (time of the activity performed) * (Weight of the user)
  //   HARDCODED MET DATA CALCULATION BASED ON ACTIVITY GIVEN
endmodule

// SPEED CALCULATOR
module Speed_Calculator (
  input  [5:0] TIME,
  input  [7:0] DISTANCE,
  output [7:0] SPEED,
  output [6:0] REMAINDER_SPEED
);

  Divider divider_1 (
    .in_1(TIME[5]), .in_2(TIME[4]), .in_3(TIME[3]), .in_4(TIME[2]), .in_5(TIME[1]), .in_6(TIME[0]),
    .in_7(DISTANCE[7]), .in_8(DISTANCE[6]), .in_9(DISTANCE[5]), .in_10(DISTANCE[4]), .in_11(DISTANCE[3]),
    .in_12(DISTANCE[2]), .in_13(DISTANCE[1]), .in_14(DISTANCE[0]), .QUOTIENT(SPEED),
    .REMAINDER(REMAINDER_SPEED));

  // Notes on the sheet:
  //   CAUTION:
  //   SPEED CALCULATOR
  //   The default value of the speed, when the inputs are showing 11111111, which is a garbage value since division of 0 / 0 is not defined
  //   Calculates the speed of the user using the formula : Speed = (Distance) / Time
endmodule

// HEARTRATE
module Heart_rate_Estimator (
  input  [7:0] SPEED,
  input  [6:0] WEIGHT,
  input  [6:0] RHR,
  output [7:0] TARGET_HR
);

  wire [7:0] adder_1_out, divider_1_quotient, divider_2_quotient;

  Divider divider_1 (
    .in_1(1'b0), .in_2(1'b0), .in_3(1'b0), .in_4(1'b0), .in_5(1'b1), .in_6(1'b0), .in_7(1'b0),
    .in_8(WEIGHT[6]), .in_9(WEIGHT[5]), .in_10(WEIGHT[4]), .in_11(WEIGHT[3]), .in_12(WEIGHT[2]),
    .in_13(WEIGHT[1]), .in_14(WEIGHT[0]), .QUOTIENT(divider_1_quotient));  // open: REMAINDER
  Adder adder_1 (.a(divider_1_quotient), .b({1'b0, RHR}), .out(adder_1_out));  // open: cin, cout
  Divider divider_2 (
    .in_1(1'b0), .in_2(1'b0), .in_3(1'b0), .in_4(1'b0), .in_5(1'b1), .in_6(1'b1), .in_7(SPEED[7]),
    .in_8(SPEED[6]), .in_9(SPEED[5]), .in_10(SPEED[4]), .in_11(SPEED[3]), .in_12(SPEED[2]), .in_13(SPEED[1]),
    .in_14(SPEED[0]), .QUOTIENT(divider_2_quotient));  // open: REMAINDER
  Adder adder_2 (.a(divider_2_quotient), .b(adder_1_out), .out(TARGET_HR));  // open: cin, cout

  // Notes on the sheet:
  //   HEART RATE ESTIMATOR
  //   Estimates the Target HR of the user using the formula: THR = RHR + (Weight / 2) + (Speed / 3)
endmodule
